# Fritzing sketch SkinnerDuino_05b (saved by Fritzing 0.9.4)
circuit board: 6.88566cm x 5.36311cm
breadboards: 1

parts:
  Arduino = Arduino Uno (Rev3) - ICSP
  N2222A = TRANSISTOR_NPN [package=to-92]
  12V = Power Jack [package=power_jack_pth_lock]
  R7 = Resistor [tolerance=±5% resistance=330 package=THT]
  R5 = Resistor [tolerance=±5% resistance=330 package=THT]
  R17 = Resistor [tolerance=±5% resistance=330 package=THT]
  OUT10 = Camdenboss CTB0158-2 [part_number=CTB0158-2 package=THT]
  OUT5 = Camdenboss CTB0158-2 [part_number=CTB0158-2 package=THT]
  R1 = Resistor [tolerance=±5% resistance=560 package=THT]
  PWR_LED = LED - 3mm [color="Green (570nm)" package="3 mm [THT]"]
  OUT6 = Camdenboss CTB0158-2 [part_number=CTB0158-2 package=THT]
  OUT9 = Camdenboss CTB0158-2 [part_number=CTB0158-2 package=THT]
  OUT3_3_3V = Camdenboss CTB0158-2 [part_number=CTB0158-2 package=THT]
  C6 = Electrolytic Capacitor [capacitance=100µF voltage=16V package="100 mil [THT, electrolytic]"]
  GND = male pin header, 4 pins [form="♂ (male)"]
  5V = male pin header, 4 pins [form="♂ (male)"]
  I2C = male pin header, 4 pins [form="♂ (male)"]
  AIO = male pin header, 4 pins [form="♂ (male)"]
  DIO = male pin header, 4 pins [form="♂ (male)"]
  GND_2 = male pin header, 4 pins [form="♂ (male)"]
  5V_2 = male pin header, 4 pins [form="♂ (male)"]
  C3 = Capacitor [part_number=104 package=cap-pth-5mm]
  C4 = Capacitor [part_number=104 package=cap-pth-5mm]
  C5 = Electrolytic Capacitor [capacitance=100µF voltage=6V package="100 mil [THT, electrolytic]"]
  LED4 = LED - 3mm [color="Red (633nm)" package="3 mm [THT]"]
  LED3 = LED - 3mm [color="Red (633nm)" package="3 mm [THT]"]
  LED2 = LED - 3mm [color="Red (633nm)" package="3 mm [THT]"]
  LED1 = LED - 3mm [color="Red (633nm)" package="3 mm [THT]"]
  LED5 = LED - 3mm [color="Red (633nm)" package="3 mm [THT]"]
  R6 = Resistor [tolerance=±5% resistance=330 package=THT]
  R8 = Resistor [tolerance=±5% resistance=10k package=THT]
  R11 = Resistor [tolerance=±5% resistance=10k package=THT]
  R9 = Resistor [tolerance=±5% resistance=10k package=THT]
  R10 = Resistor [tolerance=±5% resistance=10k package=THT]
  R2 = Resistor [tolerance=±5% resistance=330 package=THT]
  R4 = Resistor [tolerance=±5% resistance=330 package=THT]
  L293D = L293D [package=THT]

nets:
  N1: Arduino.A0, AIO.pin1
  N2: Arduino.A1, AIO.pin2
  N3: Arduino.A2, AIO.pin3
  N4: Arduino.A3, AIO.pin4
  N5: Arduino.A4/SDA, I2C.pin3
  N6: Arduino.A5/SCL, I2C.pin4
  N7: Arduino.5V, 5V.pin1, 5V.pin2, 5V.pin3, 5V.pin4, I2C.pin1, 5V_2.pin1, 5V_2.pin2, 5V_2.pin3, 5V_2.pin4, C4.2, C5.+, L293D.Enable_1, L293D.Enable_2, L293D.+V
  N8: Arduino.D8, DIO.pin1
  N9: Arduino.D9_PWM, LED3.anode, R8.Pin_0, L293D.In_3
  N10: Arduino.D10_PWM/SS, LED4.anode, R10.Pin_1, L293D.In_4
  GND: Arduino.GND, 12V.GND, R7.Pin_1, R5.Pin_1, R17.Pin_1, OUT10.pin2, OUT5.pin2, R1.Pin_1, OUT6.pin2, OUT9.pin2, OUT3_3_3V.pin2, C6.-, GND.pin1, GND.pin2, GND.pin3, GND.pin4, I2C.pin2, GND_2.pin1, GND_2.pin2, GND_2.pin3, GND_2.pin4, C3.2, C4.1, C5.-, R6.Pin_1, R8.Pin_1, R11.Pin_0, R9.Pin_1, R10.Pin_0, R4.Pin_0, L293D.0V
  N11: Arduino.D2, DIO.pin4
  N12: Arduino.D3_PWM, LED5.anode, R2.Pin_1
  N13: Arduino.D4, DIO.pin3
  N14: Arduino.D5_PWM, LED1.anode, R11.Pin_1, L293D.In_1
  N15: Arduino.D6_PWM, LED2.anode, R9.Pin_0, L293D.In_2
  N16: Arduino.D7, DIO.pin2
  N17: Arduino.3V3, N2222A.E, C3.1
  N18: N2222A.B, R2.Pin_0
  N19: N2222A.C, OUT3_3_3V.pin1
  N20: 12V.PWR, PWR_LED.anode, C6.+, L293D.+Vmotor
  N21: R7.Pin_0, LED3.cathode
  N22: R5.Pin_0, LED2.cathode
  N23: R17.Pin_0, LED1.cathode
  N24: OUT10.pin1, L293D.Out_4_(_Controlled_by_Enable_2_)
  N25: OUT5.pin1, L293D.Out_1_(_Controlled_by_Enable_1_)
  N26: R1.Pin_0, PWR_LED.cathode
  N27: OUT6.pin1, L293D.Out_2_(_Controlled_by_Enable_1_)
  N28: OUT9.pin1, L293D.Out_3_(_Controlled_by_Enable_2_)
  N29: LED4.cathode, R6.Pin_0
  N30: LED5.cathode, R4.Pin_1

notes:
  L A G 5
  Nehenemi labs
  skinnerduino
  0.5b
  2
  4
  7
  8
  +
